// Logisim project 6-Bit Arithmetic Logic Unit.circ as structural Verilog: 18 circuits, main circuit Main circuit
module Main_circuit (
  input  in_1,
  input  in_2,
  input  in_3,
  input  in_4,
  input  in_5,
  input  in_6,
  input  in_7,
  input  in_8,
  input  in_9,
  input  in_10,
  input  in_11,
  input  in_12,
  input  in_13,
  output ADDER,
  output LEFT_SHIFT,
  output BITWISE_AND,
  output BITWISE_XOR,
  output SUBTRACTOR,
  output RIGHT_SHIFT,
  output BITWISE_OR,
  output BITWISE_NOT,
  output INCREMENT,
  output DECREMENT,
  output [6:0] out_24,
  output [5:0] out_25,
  output A___B,
  output A___B_2,
  output A___B_3,
  output [11:0] out_29,
  output [5:0] Quotient,
  output [5:0] Remainder
);

  wire and_4_out, button_2_out, button_3_out, button_4_out, button_5_out, button_6_out, button_7_out,
       button_8_out, button_9_out, button_10_out, button_11_out, button_out, n6_bit_comparator_1_out_13,
       n6_bit_comparator_1_out_14, n6_bit_comparator_1_out_15, n6_bit_divider_1_divide_by_zero__error,
       not_1_out, or_1_out, or_2_out, or_3_out, or_4_out, or_5_out, or_6_out, or_7_out, or_8_out, or_9_out,
       or_10_out, parity_checker_1_x, parity_checker_2_x, t_ff_1_q, t_ff_2_q, X_out;
  wire [5:0] bitsie_or_1_out_18, bitwise_and_1_out_18, bitwise_not_1_out_7, bitwise_xor_1_out_18,
       decrement_1_out_7, left_shift_1_out_7, n6_bit_divider_1_quotient, n6_bit_divider_1_remainder,
       right_shift_1_out_7;
  wire [6:0] iincrement_1_out_7, n6_bit_adder_1_out_13, n6_bit_subtractor_1_out_13;
  wire [11:0] n6_bit_multiplier_1_out_13;

  or or_1 (or_1_out, button_5_out, button_out, button_4_out);
  or or_2 (or_2_out, button_10_out, button_4_out, button_out);
  or or_3 (or_3_out, button_5_out, button_10_out, button_out);
  or or_4 (or_4_out, button_10_out, button_5_out, button_4_out);
  _6_BIT_ADDER u_6_bit_adder_1 (
    .in_1(in_6), .in_2(in_12), .in_3(in_5), .in_4(in_11), .in_5(in_4), .in_6(in_10), .in_7(in_3),
    .in_8(in_9), .in_9(in_2), .in_10(in_8), .in_11(in_1), .in_12(in_7), .out_13(n6_bit_adder_1_out_13[0]),
    .out_14(n6_bit_adder_1_out_13[1]), .out_15(n6_bit_adder_1_out_13[2]), .out_16(n6_bit_adder_1_out_13[3]),
    .out_17(n6_bit_adder_1_out_13[4]), .out_18(n6_bit_adder_1_out_13[5]), .out_19(n6_bit_adder_1_out_13[6]));
  _6_bit_multiplier u_6_bit_multiplier_1 (
    .A0(in_6), .B0(in_12), .A1(in_5), .B1(in_11), .A2(in_4), .B2(in_10), .A3(in_3), .B3(in_9), .A4(in_2),
    .B4(in_8), .A5(in_1), .B5(in_7), .out_13(n6_bit_multiplier_1_out_13[0]),
    .out_14(n6_bit_multiplier_1_out_13[1]), .out_15(n6_bit_multiplier_1_out_13[2]),
    .out_16(n6_bit_multiplier_1_out_13[3]), .out_17(n6_bit_multiplier_1_out_13[4]),
    .out_18(n6_bit_multiplier_1_out_13[5]), .out_19(n6_bit_multiplier_1_out_13[6]),
    .out_20(n6_bit_multiplier_1_out_13[7]), .out_21(n6_bit_multiplier_1_out_13[8]),
    .out_22(n6_bit_multiplier_1_out_13[9]), .out_23(n6_bit_multiplier_1_out_13[10]),
    .out_24(n6_bit_multiplier_1_out_13[11]));
  Button button (.out(button_out));
  Button button_2 (.out(button_2_out));
  Button button_3 (.out(button_3_out));
  D_Flip_Flop d_ff_1 (.clk(button_out), .D(1'b1), .Q(ADDER), .reset(or_4_out));  // open: Qn, preset, en
  Button button_4 (.out(button_4_out));
  Button X (.out(X_out));
  Button button_5 (.out(button_5_out));
  Button button_6 (.out(button_6_out));
  Button button_7 (.out(button_7_out));
  Button button_8 (.out(button_8_out));
  D_Flip_Flop d_ff_2 (.clk(button_4_out), .D(1'b1), .Q(SUBTRACTOR), .reset(or_3_out));  // open: Qn, preset, en
  D_Flip_Flop d_ff_3 (.clk(button_2_out), .D(1'b1), .Q(LEFT_SHIFT), .reset(or_9_out));  // open: Qn, preset, en
  D_Flip_Flop d_ff_4 (.clk(button_7_out), .D(1'b1), .Q(BITWISE_OR), .reset(or_6_out));  // open: Qn, preset, en
  D_Flip_Flop d_ff_5 (.clk(button_11_out), .D(1'b1), .Q(BITWISE_NOT), .reset(or_8_out));  // open: Qn, preset, en
  Button button_9 (.out(button_9_out));
  Button button_10 (.out(button_10_out));
  Button button_11 (.out(button_11_out));
  _6_Bit_Divider u_6_bit_divider_1 (
    .Numerator({in_1, in_2, in_3, in_4, in_5, in_6}), .Denominator({in_7, in_8, in_9, in_10, in_11, in_12}),
    .Quotient(n6_bit_divider_1_quotient), .Remainder(n6_bit_divider_1_remainder),
    .Divide_by_Zero__Error(n6_bit_divider_1_divide_by_zero__error));
  _6_bit_subtractor u_6_bit_subtractor_1 (
    .A0(in_6), .B0(in_12), .A1(in_5), .B1(in_11), .A2(in_4), .B2(in_10), .A3(in_3), .B3(in_9),
    .out_13(n6_bit_subtractor_1_out_13[0]), .out_14(n6_bit_subtractor_1_out_13[1]),
    .out_15(n6_bit_subtractor_1_out_13[2]), .out_16(n6_bit_subtractor_1_out_13[3]), .A4(in_2), .B4(in_8),
    .A5(in_1), .B5(in_7), .out_17(n6_bit_subtractor_1_out_13[4]), .out_18(n6_bit_subtractor_1_out_13[5]),
    .out_19(n6_bit_subtractor_1_out_13[6]));
  D_Flip_Flop d_ff_6 (.clk(button_5_out), .D(1'b1), .Q(INCREMENT), .reset(or_2_out));  // open: Qn, preset, en
  D_Flip_Flop d_ff_7 (.clk(button_6_out), .D(1'b1), .Q(RIGHT_SHIFT), .reset(or_10_out));  // open: Qn, preset, en
  _6_bit_comparator u_6_bit_comparator_1 (
    .A0(in_6), .B0(in_12), .A1(in_5), .B1(in_11), .A2(in_4), .B2(in_10), .A3(in_3), .B3(in_9), .A4(in_2),
    .B4(in_8), .A5(in_1), .B5(in_7), .out_13(n6_bit_comparator_1_out_13),
    .out_14(n6_bit_comparator_1_out_14), .out_15(n6_bit_comparator_1_out_15));
  not not_1 (not_1_out, n6_bit_divider_1_divide_by_zero__error);
  D_Flip_Flop d_ff_8 (.clk(button_10_out), .D(1'b1), .Q(DECREMENT), .reset(or_1_out));  // open: Qn, preset, en
  D_Flip_Flop d_ff_9 (.clk(button_3_out), .D(1'b1), .Q(BITWISE_AND), .reset(or_7_out));  // open: Qn, preset, en
  D_Flip_Flop d_ff_10 (.clk(button_8_out), .D(1'b1), .Q(BITWISE_XOR), .reset(or_5_out));  // open: Qn, preset, en
  and and_1 (A___B_2, 1'b1, n6_bit_comparator_1_out_13);
  and and_2 (A___B, 1'b1, n6_bit_comparator_1_out_14);
  and and_3 (A___B_3, 1'b1, n6_bit_comparator_1_out_15);
  T_Flip_Flop t_ff_1 (.clk(button_9_out), .T(button_9_out), .Q(t_ff_1_q));  // open: Qn, preset, reset, en
  and and_4 (and_4_out, t_ff_1_q, not_1_out);
  assign Quotient = and_4_out ? n6_bit_divider_1_quotient : 6'bz;  // Controlled_Buffer controlled_buffer_1
  assign Remainder = and_4_out ? n6_bit_divider_1_remainder : 6'bz;  // Controlled_Buffer controlled_buffer_2
  assign out_29 = t_ff_2_q ? n6_bit_multiplier_1_out_13 : 12'bz;  // Controlled_Buffer controlled_buffer_3
  T_Flip_Flop t_ff_2 (.clk(X_out), .T(X_out), .Q(t_ff_2_q));  // open: Qn, preset, reset, en
  assign out_24 = ADDER ? n6_bit_adder_1_out_13 : 7'bz;  // Controlled_Buffer controlled_buffer_4
  assign out_24 = SUBTRACTOR ? n6_bit_subtractor_1_out_13 : 7'bz;  // Controlled_Buffer controlled_buffer_5
  or or_5 (or_5_out, button_3_out, button_6_out, button_7_out, button_2_out, button_11_out);
  or or_6 (or_6_out, button_3_out, button_6_out, button_11_out, button_8_out, button_2_out);
  decrement decrement_1 (
    .out_7(decrement_1_out_7[0]), .in_1(in_6), .out_8(decrement_1_out_7[1]), .in_2(in_5),
    .out_9(decrement_1_out_7[2]), .in_3(in_4), .out_10(decrement_1_out_7[3]), .in_4(in_3), .in_5(in_2),
    .out_11(decrement_1_out_7[4]), .in_6(in_1), .out_12(decrement_1_out_7[5]));  // open: out_13
  or or_7 (or_7_out, button_7_out, button_2_out, button_6_out, button_11_out, button_8_out);
  Left_Shift left_shift_1 (
    .in_1(in_6), .in_2(in_5), .in_3(in_4), .in_4(in_3), .out_7(left_shift_1_out_7[0]),
    .out_8(left_shift_1_out_7[1]), .out_9(left_shift_1_out_7[2]), .out_10(left_shift_1_out_7[3]),
    .in_5(in_2), .out_11(left_shift_1_out_7[4]), .in_6(in_1), .out_12(left_shift_1_out_7[5]));
  iincrement iincrement_1 (
    .in_1(in_6), .in_2(in_5), .in_3(in_4), .in_4(in_3), .out_7(iincrement_1_out_7[0]),
    .out_8(iincrement_1_out_7[1]), .out_9(iincrement_1_out_7[2]), .in_5(in_2), .in_6(in_1),
    .out_10(iincrement_1_out_7[3]), .out_11(iincrement_1_out_7[4]), .out_12(iincrement_1_out_7[5]),
    .out_13(iincrement_1_out_7[6]));
  or or_8 (or_8_out, button_3_out, button_6_out, button_7_out, button_2_out, button_8_out);
  or or_9 (or_9_out, button_6_out, button_7_out, button_8_out, button_3_out, button_11_out);
  or or_10 (or_10_out, button_11_out, button_3_out, button_8_out, button_7_out, button_2_out);
  Right_shift right_shift_1 (
    .in_3(in_4), .in_4(in_3), .in_5(in_2), .in_6(in_1), .in_2(in_5), .in_1(in_6),
    .out_12(right_shift_1_out_7[5]), .out_11(right_shift_1_out_7[4]), .out_10(right_shift_1_out_7[3]),
    .out_7(right_shift_1_out_7[0]), .out_8(right_shift_1_out_7[1]), .out_9(right_shift_1_out_7[2]));
  assign out_25 = LEFT_SHIFT ? left_shift_1_out_7 : 6'bz;  // Controlled_Buffer controlled_buffer_6
  Bitsie_or bitsie_or_1 (
    .A3(in_3), .B3(in_9), .A2(in_4), .B2(in_10), .A1(in_5), .B1(in_11), .A0(in_6), .B0(in_12),
    .out_15(bitsie_or_1_out_18[3]), .out_16(bitsie_or_1_out_18[2]), .out_17(bitsie_or_1_out_18[1]),
    .out_18(bitsie_or_1_out_18[0]), .A4(in_2), .B4(in_8), .B5(in_7), .A5(in_1),
    .out_13(bitsie_or_1_out_18[5]), .out_14(bitsie_or_1_out_18[4]));
  assign out_25 = RIGHT_SHIFT ? right_shift_1_out_7 : 6'bz;  // Controlled_Buffer controlled_buffer_7
  assign out_24 = INCREMENT ? iincrement_1_out_7 : 7'bz;  // Controlled_Buffer controlled_buffer_8
  Bitwise_not bitwise_not_1 (
    .in_1(in_6), .in_2(in_5), .in_3(in_4), .in_4(in_3), .out_7(bitwise_not_1_out_7[0]),
    .out_8(bitwise_not_1_out_7[1]), .out_9(bitwise_not_1_out_7[2]), .out_10(bitwise_not_1_out_7[3]),
    .in_5(in_2), .in_6(in_1), .out_11(bitwise_not_1_out_7[4]), .out_12(bitwise_not_1_out_7[5]));
  assign out_24 = DECREMENT ? {in_13, decrement_1_out_7} : 7'bz;  // Controlled_Buffer controlled_buffer_9
  // Probe on parity_checker_1_x
  // Probe on parity_checker_2_x
  Bitwise_xor bitwise_xor_1 (
    .A3(in_3), .B3(in_9), .A2(in_4), .B2(in_10), .A1(in_5), .B1(in_11), .A0(in_6), .B0(in_12),
    .out_15(bitwise_xor_1_out_18[3]), .out_16(bitwise_xor_1_out_18[2]), .out_17(bitwise_xor_1_out_18[1]),
    .out_18(bitwise_xor_1_out_18[0]), .A4(in_2), .B4(in_8), .A5(in_1), .B5(in_7),
    .out_13(bitwise_xor_1_out_18[5]), .out_14(bitwise_xor_1_out_18[4]));
  Parity_Checker parity_checker_1 (
    .A0(in_6), .A1(in_5), .A2(in_4), .A3(in_3), .A4(in_2), .A5(in_1), .X(parity_checker_1_x));
  Parity_Checker parity_checker_2 (
    .A0(in_12), .A1(in_11), .A2(in_10), .A3(in_9), .A4(in_8), .A5(in_7), .X(parity_checker_2_x));
  Bitwise_and bitwise_and_1 (
    .A3(in_3), .B3(in_9), .A2(in_4), .B2(in_10), .A1(in_11), .B1(in_5), .A0(in_12), .B0(in_6),
    .out_15(bitwise_and_1_out_18[3]), .out_16(bitwise_and_1_out_18[2]), .out_17(bitwise_and_1_out_18[1]),
    .out_18(bitwise_and_1_out_18[0]), .B4(in_2), .A4(in_8), .A5(in_7), .B5(in_1),
    .out_13(bitwise_and_1_out_18[5]), .out_14(bitwise_and_1_out_18[4]));
  assign out_25 = BITWISE_NOT ? bitwise_not_1_out_7 : 6'bz;  // Controlled_Buffer controlled_buffer_10
  assign out_25 = BITWISE_AND ? bitwise_and_1_out_18 : 6'bz;  // Controlled_Buffer controlled_buffer_11
  assign out_25 = BITWISE_OR ? bitsie_or_1_out_18 : 6'bz;  // Controlled_Buffer controlled_buffer_12
  assign out_25 = BITWISE_XOR ? bitwise_xor_1_out_18 : 6'bz;  // Controlled_Buffer controlled_buffer_13

  // Notes on the sheet:
  //   INSTRUCTIONS:
  //    - There are four output windows in the program:
  //    - All urinary operators are performed on input A.
  //   MADE BY: 
  //    - This is a binary ALU in which you will enter (either 2 or 1) 6-bit binary numbers.
  //    - This ALU comprises of two types of operations: Binary & Urinary
  //    - There are designated buttons for each output which work on on/off logic.
  //   2. Output window 02 shows output for left and right shift and bitwise operations.
  //   3. Output window 03 shows output for multilplication (12-bit output).
  //   - All binary operators have the left operand as A and right operand as B.
  //    - Comparision and parity check will always be shown in the output.
  //    - Binary Operations include: Add, Subtract, Multiply, Divide, Compare, and binary bitwise operations.
  //    - Urinary Operations include: Left and right shift, increment, decrement, and urinary bitwise operations.
  //    - The opearations which have the same output window cannot be activated simultaneously.
  //   1. Output window 01 shows output for addition, subtraction, increment, and decrement.
  //    - If B is zero as the denominator in division then output will not be active unless B is not equal to zero.
  //   4. Output window 04 shows two outputs for division (one output displays the quotient while the other displays the remainder).
  //   SYED MUHAMMAD SUFYAN (24K-0806)
  //   FAIZAN BASHEER (24K-0569)
  //   6 - BIT ARITHMETIC LOGIC UNIT 
  //   ABDUR REHMAN KHAN (24K-0767) - GROUP LEADER
  //   0 FOR EVEN PARITY OR 1 FOR ODD PARITY
  //   INPUT CONTROL
  //   32  16   8     4     2    1
  //   32  16   8     4     2    1
  //   A5  A4   A3  A2   A1  A0
  //   B5  B4  B3  B2  B1 B0
  //   COMPARISION BETWEEN A & B
  //   WINDOW 01 Activated Outputs
  //   OUTPUT WINDOWS
  //   OUTPUT WINDOW 01
  //   OUTPUT WINDOW 03
  //   WINDOW 02 Activated Outputs
  //   OUTPUT WINDOW 02
  //   OUTPUT WINDOW 04
  //   PARITY CHECK FOR A
  //   PARITY CHECK FOR B
  //   0 FOR EVEN PARITY OR 1 FOR ODD PARITY
endmodule

module _6_BIT_ADDER (
  input  in_1,
  input  in_2,
  input  in_3,
  input  in_4,
  input  in_5,
  input  in_6,
  input  in_7,
  input  in_8,
  input  in_9,
  input  in_10,
  input  in_11,
  input  in_12,
  output out_13,
  output out_14,
  output out_15,
  output out_16,
  output out_17,
  output out_18,
  output out_19
);

  wire full_adder_1_out_5, full_adder_2_out_5, full_adder_3_out_5, full_adder_4_out_5, half_adder_1_out_4;

  full_adder full_adder_1 (
    .in_1(half_adder_1_out_4), .in_2(in_3), .in_3(in_4), .out_4(out_14), .out_5(full_adder_1_out_5));
  Half_adder half_adder_1 (.in_1(in_1), .in_2(in_2), .out_3(out_13), .out_4(half_adder_1_out_4));
  full_adder full_adder_2 (
    .in_1(full_adder_1_out_5), .in_2(in_5), .in_3(in_6), .out_4(out_15), .out_5(full_adder_2_out_5));
  full_adder full_adder_3 (
    .in_1(full_adder_2_out_5), .in_2(in_7), .in_3(in_8), .out_4(out_16), .out_5(full_adder_3_out_5));
  full_adder full_adder_4 (
    .in_1(full_adder_3_out_5), .in_2(in_9), .in_3(in_10), .out_4(out_17), .out_5(full_adder_4_out_5));
  full_adder full_adder_5 (.in_1(full_adder_4_out_5), .in_2(in_11), .in_3(in_12), .out_4(out_18), .out_5(out_19));
endmodule

module _6_bit_subtractor (
  input  A0,
  input  B0,
  input  A1,
  input  B1,
  input  A2,
  input  B2,
  input  A3,
  input  B3,
  input  A4,
  input  B4,
  input  A5,
  input  B5,
  output out_13,
  output out_14,
  output out_15,
  output out_16,
  output out_17,
  output out_18,
  output out_19
);

  wire full_adder_1_out_5, full_adder_2_out_5, full_adder_3_out_5, full_adder_4_out_5, full_adder_5_out_5,
       full_adder_6_out_5, xor_1_out, xor_2_out, xor_3_out, xor_4_out, xor_5_out, xor_6_out;

  xor xor_1 (xor_1_out, B0, 1'b1);
  xor xor_2 (xor_2_out, B1, 1'b1);
  xor xor_3 (xor_3_out, 1'b1, B2);
  xor xor_4 (xor_4_out, 1'b1, B3);
  xor xor_5 (xor_5_out, 1'b1, B4);
  xor xor_6 (xor_6_out, 1'b1, B5);
  full_adder full_adder_1 (.in_1(A0), .in_2(1'b1), .in_3(xor_1_out), .out_4(out_13), .out_5(full_adder_1_out_5));
  full_adder full_adder_2 (
    .in_1(A1), .in_2(xor_2_out), .in_3(full_adder_1_out_5), .out_4(out_14), .out_5(full_adder_2_out_5));
  full_adder full_adder_3 (
    .in_1(A2), .in_2(xor_3_out), .in_3(full_adder_2_out_5), .out_4(out_15), .out_5(full_adder_3_out_5));
  full_adder full_adder_4 (
    .in_1(A3), .in_2(xor_4_out), .in_3(full_adder_3_out_5), .out_4(out_16), .out_5(full_adder_4_out_5));
  full_adder full_adder_5 (
    .in_1(A4), .in_2(xor_5_out), .in_3(full_adder_4_out_5), .out_4(out_17), .out_5(full_adder_5_out_5));
  full_adder full_adder_6 (
    .in_1(A5), .in_2(xor_6_out), .in_3(full_adder_5_out_5), .out_4(out_18), .out_5(full_adder_6_out_5));
  xor xor_7 (out_19, full_adder_5_out_5, full_adder_6_out_5);

  // Notes on the sheet:
  //   C0
endmodule

module _6_bit_multiplier (
  input  A0,
  input  B0,
  input  A1,
  input  B1,
  input  A2,
  input  B2,
  input  A3,
  input  B3,
  input  A4,
  input  B4,
  input  A5,
  input  B5,
  output out_13,
  output out_14,
  output out_15,
  output out_16,
  output out_17,
  output out_18,
  output out_19,
  output out_20,
  output out_21,
  output out_22,
  output out_23,
  output out_24
);

  wire and_2_out, and_3_out, and_4_out, and_5_out, and_6_out, and_7_out, and_8_out, and_9_out, and_10_out,
       and_11_out, and_12_out, and_13_out, and_14_out, and_15_out, and_16_out, and_17_out, and_18_out,
       and_19_out, and_20_out, and_21_out, and_22_out, and_23_out, and_24_out, and_25_out, and_26_out,
       and_27_out, and_28_out, and_29_out, and_30_out, and_31_out, and_32_out, and_33_out, and_34_out,
       and_35_out, and_36_out, full_adder_1_out_4, full_adder_1_out_5, full_adder_2_out_4,
       full_adder_2_out_5, full_adder_3_out_4, full_adder_3_out_5, full_adder_4_out_4, full_adder_4_out_5,
       full_adder_5_out_4, full_adder_5_out_5, full_adder_6_out_4, full_adder_6_out_5, full_adder_7_out_4,
       full_adder_7_out_5, full_adder_8_out_5, full_adder_9_out_4, full_adder_9_out_5, full_adder_10_out_4,
       full_adder_10_out_5, full_adder_11_out_4, full_adder_11_out_5, full_adder_12_out_4,
       full_adder_12_out_5, full_adder_13_out_4, full_adder_13_out_5, full_adder_14_out_4,
       full_adder_14_out_5, full_adder_15_out_4, full_adder_15_out_5, full_adder_17_out_4,
       full_adder_17_out_5, full_adder_18_out_4, full_adder_18_out_5, full_adder_19_out_4,
       full_adder_19_out_5, full_adder_20_out_4, full_adder_20_out_5, full_adder_21_out_5,
       full_adder_22_out_5, full_adder_23_out_4, full_adder_23_out_5, full_adder_24_out_5,
       half_adder_1_out_4, half_adder_2_out_3, half_adder_2_out_4, half_adder_3_out_4, half_adder_4_out_4,
       half_adder_5_out_4, half_adder_6_out_4;

  and and_1 (out_13, A0, B0);
  and and_2 (and_2_out, A1, B0);
  and and_3 (and_3_out, A0, B1);
  and and_4 (and_4_out, A2, B0);
  and and_5 (and_5_out, A1, B1);
  and and_6 (and_6_out, A0, B2);
  and and_7 (and_7_out, A3, B0);
  and and_8 (and_8_out, A2, B1);
  and and_9 (and_9_out, A1, B2);
  and and_10 (and_10_out, A0, B3);
  and and_11 (and_11_out, A4, B0);
  and and_12 (and_12_out, A3, B1);
  and and_13 (and_13_out, A2, B2);
  and and_14 (and_14_out, A1, B3);
  and and_15 (and_15_out, A0, B4);
  and and_16 (and_16_out, A5, B0);
  and and_17 (and_17_out, A4, B1);
  and and_18 (and_18_out, A3, B2);
  and and_19 (and_19_out, A2, B3);
  and and_20 (and_20_out, A1, B4);
  and and_21 (and_21_out, A0, B5);
  and and_22 (and_22_out, A4, B2);
  and and_23 (and_23_out, A3, B3);
  and and_24 (and_24_out, A2, B4);
  and and_25 (and_25_out, A1, B5);
  and and_26 (and_26_out, A5, B2);
  and and_27 (and_27_out, A4, B3);
  and and_28 (and_28_out, A3, B4);
  and and_29 (and_29_out, A2, B5);
  and and_30 (and_30_out, A5, B3);
  and and_31 (and_31_out, A4, B4);
  and and_32 (and_32_out, A3, B5);
  and and_33 (and_33_out, A5, B4);
  and and_34 (and_34_out, A4, B5);
  and and_35 (and_35_out, A5, B5);
  and and_36 (and_36_out, A5, B1);
  full_adder full_adder_1 (
    .in_1(and_30_out), .in_2(and_31_out), .in_3(and_32_out), .out_4(full_adder_1_out_4),
    .out_5(full_adder_1_out_5));
  full_adder full_adder_2 (
    .in_1(and_11_out), .in_2(and_12_out), .in_3(and_13_out), .out_4(full_adder_2_out_4),
    .out_5(full_adder_2_out_5));
  full_adder full_adder_3 (
    .in_1(and_19_out), .in_2(and_20_out), .in_3(and_21_out), .out_4(full_adder_3_out_4),
    .out_5(full_adder_3_out_5));
  full_adder full_adder_4 (
    .in_1(and_22_out), .in_2(and_23_out), .in_3(and_24_out), .out_4(full_adder_4_out_4),
    .out_5(full_adder_4_out_5));
  full_adder full_adder_5 (
    .in_1(and_26_out), .in_2(and_27_out), .in_3(and_28_out), .out_4(full_adder_5_out_4),
    .out_5(full_adder_5_out_5));
  full_adder full_adder_6 (
    .in_1(and_16_out), .in_2(and_17_out), .in_3(and_18_out), .out_4(full_adder_6_out_4),
    .out_5(full_adder_6_out_5));
  full_adder full_adder_7 (
    .in_1(and_33_out), .in_2(and_34_out), .in_3(full_adder_1_out_5), .out_4(full_adder_7_out_4),
    .out_5(full_adder_7_out_5));
  full_adder full_adder_8 (
    .in_1(half_adder_2_out_3), .in_2(and_6_out), .in_3(half_adder_1_out_4), .out_4(out_15),
    .out_5(full_adder_8_out_5));
  full_adder full_adder_9 (
    .in_1(and_7_out), .in_2(and_8_out), .in_3(and_9_out), .out_4(full_adder_9_out_4),
    .out_5(full_adder_9_out_5));
  full_adder full_adder_10 (
    .in_1(and_14_out), .in_2(and_15_out), .in_3(full_adder_14_out_5), .out_4(full_adder_10_out_4),
    .out_5(full_adder_10_out_5));
  full_adder full_adder_11 (
    .in_1(full_adder_4_out_4), .in_2(and_25_out), .in_3(and_36_out), .out_4(full_adder_11_out_4),
    .out_5(full_adder_11_out_5));
  Half_adder half_adder_1 (.in_1(and_2_out), .in_2(and_3_out), .out_3(out_14), .out_4(half_adder_1_out_4));
  Half_adder half_adder_2 (.in_1(and_4_out), .in_2(and_5_out), .out_3(half_adder_2_out_3), .out_4(half_adder_2_out_4));
  full_adder full_adder_12 (
    .in_1(full_adder_6_out_4), .in_2(full_adder_3_out_4), .in_3(full_adder_2_out_5),
    .out_4(full_adder_12_out_4), .out_5(full_adder_12_out_5));
  full_adder full_adder_13 (
    .in_1(full_adder_4_out_5), .in_2(full_adder_11_out_5), .in_3(and_29_out), .out_4(full_adder_13_out_4),
    .out_5(full_adder_13_out_5));
  full_adder full_adder_14 (
    .in_1(full_adder_8_out_5), .in_2(half_adder_2_out_4), .in_3(full_adder_9_out_4),
    .out_4(full_adder_14_out_4), .out_5(full_adder_14_out_5));
  full_adder full_adder_15 (
    .in_1(full_adder_5_out_5), .in_2(full_adder_1_out_4), .in_3(full_adder_13_out_5),
    .out_4(full_adder_15_out_4), .out_5(full_adder_15_out_5));
  full_adder full_adder_16 (
    .in_1(full_adder_7_out_5), .in_2(and_35_out), .in_3(full_adder_21_out_5), .out_4(out_23), .out_5(out_24));
  full_adder full_adder_17 (
    .in_1(full_adder_10_out_4), .in_2(half_adder_3_out_4), .in_3(full_adder_2_out_4),
    .out_4(full_adder_17_out_4), .out_5(full_adder_17_out_5));
  full_adder full_adder_18 (
    .in_1(full_adder_12_out_5), .in_2(full_adder_3_out_5), .in_3(full_adder_6_out_5),
    .out_4(full_adder_18_out_4), .out_5(full_adder_18_out_5));
  full_adder full_adder_19 (
    .in_1(full_adder_5_out_4), .in_2(full_adder_13_out_4), .in_3(full_adder_18_out_5),
    .out_4(full_adder_19_out_4), .out_5(full_adder_19_out_5));
  full_adder full_adder_20 (
    .in_1(full_adder_12_out_4), .in_2(full_adder_17_out_5), .in_3(full_adder_10_out_5),
    .out_4(full_adder_20_out_4), .out_5(full_adder_20_out_5));
  full_adder full_adder_21 (
    .in_1(full_adder_7_out_4), .in_2(full_adder_15_out_5), .in_3(full_adder_22_out_5), .out_4(out_22),
    .out_5(full_adder_21_out_5));
  full_adder full_adder_22 (
    .in_1(full_adder_15_out_4), .in_2(full_adder_19_out_5), .in_3(full_adder_24_out_5), .out_4(out_21),
    .out_5(full_adder_22_out_5));
  full_adder full_adder_23 (
    .in_1(full_adder_18_out_4), .in_2(full_adder_11_out_4), .in_3(half_adder_5_out_4),
    .out_4(full_adder_23_out_4), .out_5(full_adder_23_out_5));
  Half_adder half_adder_3 (.in_1(full_adder_14_out_4), .in_2(and_10_out), .out_3(out_16), .out_4(half_adder_3_out_4));
  Half_adder half_adder_4 (
    .in_1(full_adder_17_out_4), .in_2(full_adder_9_out_5), .out_3(out_17), .out_4(half_adder_4_out_4));
  Half_adder half_adder_5 (
    .in_1(full_adder_20_out_4), .in_2(half_adder_4_out_4), .out_3(out_18), .out_4(half_adder_5_out_4));
  full_adder full_adder_24 (
    .in_1(half_adder_6_out_4), .in_2(full_adder_23_out_5), .in_3(full_adder_19_out_4), .out_4(out_20),
    .out_5(full_adder_24_out_5));
  Half_adder half_adder_6 (
    .in_1(full_adder_23_out_4), .in_2(full_adder_20_out_5), .out_3(out_19), .out_4(half_adder_6_out_4));
endmodule

module _6_Bit_Divider (
  input  [5:0] Numerator,
  input  [5:0] Denominator,
  output [5:0] Quotient,
  output [5:0] Remainder,
  output Divide_by_Zero__Error
);

  wire comparator_1_lt, pull_resistor_2_node, pull_resistor_3_node, pull_resistor_4_node,
       pull_resistor_5_node, pull_resistor_6_node, pull_resistor_7_node, subtractor_1_bout,
       subtractor_2_bout, subtractor_3_bout, subtractor_4_bout, subtractor_5_bout, subtractor_6_bout,
       zero6_2_p2, zero6_3_p2, zero6_4_p2, zero6_5_p2, zero6_6_p2, zero6_7_p2;
  wire [2:0] pull_resistor_1_node, pull_resistor_1_node_2;
  wire [5:0] and_6_out, multiplexer_1_out, multiplexer_2_out, multiplexer_3_out, multiplexer_4_out,
       multiplexer_6_out, subtractor_1_out, subtractor_2_out, subtractor_3_out, subtractor_4_out,
       subtractor_5_out, subtractor_6_out;

  Comparator #(.width(6), .mode("unsigned")) comparator_1 (
    .a(Numerator), .b(Denominator), .lt(comparator_1_lt));  // open: gt, eq
  Pull_Resistor pull_resistor_1 (.node({pull_resistor_1_node_2, pull_resistor_1_node}));
  // Divider_Zero6 zero6_1: pin names not known; wires that end beside it: Denominator, Divide_by_Zero__Error
  Pull_Resistor pull_resistor_2 (.node(pull_resistor_2_node));
  Subtractor #(.width(6)) subtractor_1 (
    .a(Numerator), .b({Denominator[0], pull_resistor_1_node_2, pull_resistor_1_node[2:1]}),
    .out(subtractor_1_out), .bin(pull_resistor_2_node), .bout(subtractor_1_bout));
  and and_1 (and_6_out[5], ~subtractor_1_bout, zero6_2_p2);  // AND_Gate
  // Divider_Zero6 zero6_2: pin names not known; wires that end beside it: {1'b0, Denominator[5:1]}, zero6_2_p2
  Multiplexer #(.width(6), .enable("false")) multiplexer_1 (
    .in0(Numerator), .in1(subtractor_1_out), .out(multiplexer_1_out), .sel(and_6_out[5]));
  Pull_Resistor pull_resistor_3 (.node(pull_resistor_3_node));
  Subtractor #(.width(6)) subtractor_2 (
    .a(multiplexer_1_out), .b({Denominator[1:0], pull_resistor_1_node_2, pull_resistor_1_node[2]}),
    .out(subtractor_2_out), .bin(pull_resistor_3_node), .bout(subtractor_2_bout));
  // Divider_Zero6 zero6_3: pin names not known; wires that end beside it: {2'b00, Denominator[5:2]}, zero6_3_p2
  and and_2 (and_6_out[4], ~subtractor_2_bout, zero6_3_p2);  // AND_Gate
  Multiplexer #(.width(6), .enable("false")) multiplexer_2 (
    .in0(multiplexer_1_out), .in1(subtractor_2_out), .out(multiplexer_2_out), .sel(and_6_out[4]));
  Pull_Resistor pull_resistor_4 (.node(pull_resistor_4_node));
  Subtractor #(.width(6)) subtractor_3 (
    .a(multiplexer_2_out), .b({Denominator[2:0], pull_resistor_1_node_2}), .out(subtractor_3_out),
    .bin(pull_resistor_4_node), .bout(subtractor_3_bout));
  // Divider_Zero6 zero6_4: pin names not known; wires that end beside it: {3'b000, Denominator[5:3]}, zero6_4_p2
  and and_3 (and_6_out[3], ~subtractor_3_bout, zero6_4_p2);  // AND_Gate
  Multiplexer #(.width(6), .enable("false")) multiplexer_3 (
    .in0(multiplexer_2_out), .in1(subtractor_3_out), .out(multiplexer_3_out), .sel(and_6_out[3]));
  Pull_Resistor pull_resistor_5 (.node(pull_resistor_5_node));
  // Divider_Zero6 zero6_5: pin names not known; wires that end beside it: {4'b0000, Denominator[5:4]}, zero6_5_p2
  Subtractor #(.width(6)) subtractor_4 (
    .a(multiplexer_3_out), .b({Denominator[3:0], pull_resistor_1_node_2[2:1]}), .out(subtractor_4_out),
    .bin(pull_resistor_5_node), .bout(subtractor_4_bout));
  and and_4 (and_6_out[2], ~subtractor_4_bout, zero6_5_p2);  // AND_Gate
  Multiplexer #(.width(6), .enable("false")) multiplexer_4 (
    .in0(multiplexer_3_out), .in1(subtractor_4_out), .out(multiplexer_4_out), .sel(and_6_out[2]));
  Pull_Resistor pull_resistor_6 (.node(pull_resistor_6_node));
  // Divider_Zero6 zero6_6: pin names not known; wires that end beside it: {{5{1'b0}}, Denominator[5]}, zero6_6_p2
  Subtractor #(.width(6)) subtractor_5 (
    .a(multiplexer_4_out), .b({Denominator[4:0], pull_resistor_1_node_2[2]}), .out(subtractor_5_out),
    .bin(pull_resistor_6_node), .bout(subtractor_5_bout));
  and and_5 (and_6_out[1], ~subtractor_5_bout, zero6_6_p2);  // AND_Gate
  Multiplexer #(.width(6), .enable("false")) multiplexer_5 (
    .in0(and_6_out), .in1({6{1'b0}}), .out(Quotient), .sel(comparator_1_lt));
  Multiplexer #(.width(6), .enable("false")) multiplexer_6 (
    .in0(multiplexer_4_out), .in1(subtractor_5_out), .out(multiplexer_6_out), .sel(and_6_out[1]));
  Pull_Resistor pull_resistor_7 (.node(pull_resistor_7_node));
  Subtractor #(.width(6)) subtractor_6 (
    .a(multiplexer_6_out), .b(Denominator), .out(subtractor_6_out), .bin(pull_resistor_7_node),
    .bout(subtractor_6_bout));
  and and_6 (and_6_out[0], ~subtractor_6_bout, zero6_7_p2);  // AND_Gate
  // Divider_Zero6 zero6_7: pin names not known; wires that end beside it: {6{1'b0}}, zero6_7_p2
  Multiplexer #(.width(6), .enable("false")) multiplexer_7 (
    .in0(multiplexer_6_out), .in1(subtractor_6_out), .out(Remainder), .sel(and_6_out[0]));

  // Notes on the sheet:
  //   If Zero, Quotient will contain all 1's. Remainder will be Numerator.
  //   If N<D, the Quotient will be 0. Remainder will be Numerator
  //   6 Bit Divider Circuit
endmodule

module _6_bit_comparator (
  input  A0,
  input  B0,
  input  A1,
  input  B1,
  input  A2,
  input  B2,
  input  A3,
  input  B3,
  input  A4,
  input  B4,
  input  A5,
  input  B5,
  output out_13,
  output out_14,
  output out_15
);

  wire and_1_out, and_2_out, and_3_out, and_4_out, and_5_out, and_6_out, and_7_out, and_8_out, and_9_out,
       and_10_out, and_11_out, and_12_out, and_14_out, and_15_out, and_16_out, and_17_out, and_18_out,
       and_19_out, and_20_out, and_21_out, and_22_out, and_23_out, not_1_out, not_2_out, not_3_out,
       not_4_out, not_5_out, not_6_out, not_7_out, not_8_out, not_9_out, not_10_out, not_11_out, not_12_out,
       xnor_1_out, xnor_2_out, xnor_3_out, xnor_4_out, xnor_5_out, xnor_6_out;

  not not_1 (not_1_out, A5);
  not not_2 (not_2_out, B5);
  not not_3 (not_3_out, B1);
  not not_4 (not_4_out, B0);
  not not_5 (not_5_out, A4);
  not not_6 (not_6_out, A2);
  not not_7 (not_7_out, A1);
  not not_8 (not_8_out, A0);
  not not_9 (not_9_out, B4);
  not not_10 (not_10_out, B3);
  not not_11 (not_11_out, B2);
  not not_12 (not_12_out, A3);
  xnor xnor_1 (xnor_1_out, A0, B0);
  xnor xnor_2 (xnor_2_out, A1, B1);
  xnor xnor_3 (xnor_3_out, A2, B2);
  xnor xnor_4 (xnor_4_out, A3, B3);
  xnor xnor_5 (xnor_5_out, A4, B4);
  xnor xnor_6 (xnor_6_out, A5, B5);
  and and_1 (and_1_out, not_1_out, B5);
  and and_2 (and_2_out, not_5_out, B4);
  and and_3 (and_3_out, not_12_out, B3);
  and and_4 (and_4_out, not_6_out, B2);
  and and_5 (and_5_out, not_7_out, B1);
  and and_6 (and_6_out, not_8_out, B0);
  and and_7 (and_7_out, A5, not_2_out);
  and and_8 (and_8_out, A4, not_9_out);
  and and_9 (and_9_out, A3, not_10_out);
  and and_10 (and_10_out, A2, not_11_out);
  and and_11 (and_11_out, A1, not_3_out);
  and and_12 (and_12_out, A0, not_4_out);
  and and_13 (out_13, xnor_1_out, xnor_2_out, xnor_3_out, xnor_4_out, xnor_5_out, xnor_6_out);
  and and_14 (and_14_out, xnor_6_out, and_8_out);
  and and_15 (and_15_out, xnor_6_out, xnor_5_out, and_9_out);
  and and_16 (and_16_out, xnor_4_out, xnor_5_out, xnor_6_out, and_10_out);
  and and_17 (and_17_out, xnor_3_out, xnor_4_out, xnor_5_out, xnor_6_out, and_11_out);
  and and_18 (and_18_out, xnor_2_out, xnor_3_out, xnor_4_out, xnor_5_out, xnor_6_out, and_12_out);
  and and_19 (and_19_out, xnor_6_out, and_2_out);
  and and_20 (and_20_out, xnor_6_out, xnor_5_out, and_3_out);
  and and_21 (and_21_out, xnor_4_out, xnor_6_out, xnor_5_out, and_4_out);
  and and_22 (and_22_out, xnor_6_out, xnor_5_out, xnor_4_out, xnor_3_out, and_5_out);
  and and_23 (and_23_out, xnor_2_out, xnor_6_out, xnor_5_out, xnor_4_out, xnor_3_out, and_6_out);
  or or_1 (out_15, and_7_out, and_14_out, and_15_out, and_16_out, and_17_out, and_18_out);
  or or_2 (out_14, and_1_out, and_19_out, and_20_out, and_21_out, and_22_out, and_23_out);
endmodule

module Left_Shift (
  input  in_1,
  input  in_2,
  input  in_3,
  input  in_4,
  input  in_5,
  input  in_6,
  output out_7,
  output out_8,
  output out_9,
  output out_10,
  output out_11,
  output out_12
);

  wire and_1_out, and_2_out, and_3_out, and_4_out, and_5_out, and_6_out, and_7_out, and_8_out, and_9_out,
       and_10_out, and_11_out, and_12_out, not_1_out, not_2_out, not_3_out, not_4_out, not_5_out, not_6_out;

  not not_1 (not_1_out, 1'b1);
  not not_2 (not_2_out, 1'b1);
  not not_3 (not_3_out, 1'b1);
  not not_4 (not_4_out, 1'b1);
  not not_5 (not_5_out, 1'b1);
  not not_6 (not_6_out, 1'b1);
  and and_1 (and_1_out, 1'b0, 1'b1);
  and and_2 (and_2_out, not_3_out, in_1);
  and and_3 (and_3_out, 1'b1, in_1);
  and and_4 (and_4_out, not_4_out, in_2);
  and and_5 (and_5_out, 1'b1, in_2);
  and and_6 (and_6_out, not_5_out, in_3);
  and and_7 (and_7_out, 1'b1, in_3);
  and and_8 (and_8_out, not_1_out, in_4);
  and and_9 (and_9_out, 1'b1, in_4);
  and and_10 (and_10_out, not_6_out, in_5);
  and and_11 (and_11_out, 1'b1, in_5);
  and and_12 (and_12_out, not_2_out, in_6);
  or or_1 (out_7, and_1_out, and_2_out);
  or or_2 (out_8, and_3_out, and_4_out);
  or or_3 (out_9, and_5_out, and_6_out);
  or or_4 (out_10, and_7_out, and_8_out);
  or or_5 (out_11, and_9_out, and_10_out);
  or or_6 (out_12, and_11_out, and_12_out);
endmodule

module Right_shift (
  input  in_1,
  input  in_2,
  input  in_3,
  input  in_4,
  input  in_5,
  input  in_6,
  output out_7,
  output out_8,
  output out_9,
  output out_10,
  output out_11,
  output out_12
);

  wire and_1_out, and_2_out, and_3_out, and_4_out, and_5_out, and_6_out, and_7_out, and_8_out, and_9_out,
       and_10_out, and_11_out, and_12_out, not_1_out, not_2_out, not_3_out, not_4_out, not_5_out, not_6_out;

  not not_1 (not_1_out, 1'b1);
  not not_2 (not_2_out, 1'b1);
  not not_3 (not_3_out, 1'b1);
  not not_4 (not_4_out, 1'b1);
  not not_5 (not_5_out, 1'b1);
  and and_1 (and_1_out, not_1_out, in_3);
  and and_2 (and_2_out, 1'b1, in_4);
  and and_3 (and_3_out, not_3_out, in_4);
  and and_4 (and_4_out, 1'b1, in_5);
  and and_5 (and_5_out, not_4_out, in_5);
  and and_6 (and_6_out, 1'b1, in_6);
  and and_7 (and_7_out, not_5_out, in_6);
  and and_8 (and_8_out, 1'b1, 1'b0);
  and and_9 (and_9_out, not_2_out, in_2);
  and and_10 (and_10_out, 1'b1, in_3);
  not not_6 (not_6_out, 1'b1);
  or or_1 (out_8, and_9_out, and_10_out);
  or or_2 (out_9, and_1_out, and_2_out);
  or or_3 (out_10, and_3_out, and_4_out);
  or or_4 (out_11, and_5_out, and_6_out);
  or or_5 (out_12, and_7_out, and_8_out);
  and and_11 (and_11_out, not_6_out, in_1);
  and and_12 (and_12_out, 1'b1, in_2);
  or or_6 (out_7, and_11_out, and_12_out);
endmodule

module iincrement (
  input  in_1,
  input  in_2,
  input  in_3,
  input  in_4,
  input  in_5,
  input  in_6,
  output out_7,
  output out_8,
  output out_9,
  output out_10,
  output out_11,
  output out_12,
  output out_13
);

  wire half_adder_1_out_4, half_adder_2_out_4, half_adder_3_out_4, half_adder_4_out_4, half_adder_5_out_4;

  Half_adder half_adder_1 (.in_1(1'b1), .in_2(in_1), .out_3(out_7), .out_4(half_adder_1_out_4));
  Half_adder half_adder_2 (.in_1(half_adder_1_out_4), .in_2(in_2), .out_3(out_8), .out_4(half_adder_2_out_4));
  Half_adder half_adder_3 (.in_1(half_adder_2_out_4), .in_2(in_3), .out_3(out_9), .out_4(half_adder_3_out_4));
  Half_adder half_adder_4 (.in_1(half_adder_3_out_4), .in_2(in_4), .out_3(out_10), .out_4(half_adder_4_out_4));
  Half_adder half_adder_5 (.in_1(half_adder_4_out_4), .in_2(in_5), .out_3(out_11), .out_4(half_adder_5_out_4));
  Half_adder half_adder_6 (.in_1(half_adder_5_out_4), .in_2(in_6), .out_3(out_12), .out_4(out_13));
endmodule

module decrement (
  input  in_1,
  input  in_2,
  input  in_3,
  input  in_4,
  input  in_5,
  input  in_6,
  output out_7,
  output out_8,
  output out_9,
  output out_10,
  output out_11,
  output out_12,
  output out_13
);

  wire full_adder_1_out_5, full_adder_2_out_5, full_adder_3_out_5, full_adder_4_out_5, half_adder_1_out_4;

  full_adder full_adder_1 (
    .in_1(1'b1), .in_2(in_2), .in_3(half_adder_1_out_4), .out_4(out_8), .out_5(full_adder_1_out_5));
  full_adder full_adder_2 (
    .in_1(1'b1), .in_2(in_3), .in_3(full_adder_1_out_5), .out_4(out_9), .out_5(full_adder_2_out_5));
  Half_adder half_adder_1 (.in_1(1'b1), .in_2(in_1), .out_3(out_7), .out_4(half_adder_1_out_4));
  full_adder full_adder_3 (
    .in_1(1'b1), .in_2(in_4), .in_3(full_adder_2_out_5), .out_4(out_10), .out_5(full_adder_3_out_5));
  full_adder full_adder_4 (
    .in_1(1'b1), .in_2(in_5), .in_3(full_adder_3_out_5), .out_4(out_11), .out_5(full_adder_4_out_5));
  full_adder full_adder_5 (.in_1(1'b1), .in_2(in_6), .in_3(full_adder_4_out_5), .out_4(out_12), .out_5(out_13));
endmodule

module Bitwise_and (
  input  B5,
  input  A5,
  input  B4,
  input  A4,
  input  A3,
  input  B3,
  input  A2,
  input  B2,
  input  A1,
  input  B1,
  input  A0,
  input  B0,
  output out_13,
  output out_14,
  output out_15,
  output out_16,
  output out_17,
  output out_18
);

  and and_1 (out_13, B5, A5);
  and and_2 (out_14, B4, A4);
  and and_3 (out_15, A3, B3);
  and and_4 (out_16, A2, B2);
  and and_5 (out_17, A1, B1);
  and and_6 (out_18, A0, B0);
endmodule

module Bitsie_or (
  input  A5,
  input  B5,
  input  A4,
  input  B4,
  input  A3,
  input  B3,
  input  A2,
  input  B2,
  input  A1,
  input  B1,
  input  A0,
  input  B0,
  output out_13,
  output out_14,
  output out_15,
  output out_16,
  output out_17,
  output out_18
);

  or or_1 (out_13, A5, B5);
  or or_2 (out_14, A4, B4);
  or or_3 (out_15, A3, B3);
  or or_4 (out_16, A2, B2);
  or or_5 (out_17, A1, B1);
  or or_6 (out_18, A0, B0);
endmodule

module Bitwise_xor (
  input  A5,
  input  B5,
  input  A4,
  input  B4,
  input  A3,
  input  B3,
  input  A2,
  input  B2,
  input  A1,
  input  B1,
  input  A0,
  input  B0,
  output out_13,
  output out_14,
  output out_15,
  output out_16,
  output out_17,
  output out_18
);

  xor xor_1 (out_13, A5, B5);
  xor xor_2 (out_14, A4, B4);
  xor xor_3 (out_15, A3, B3);
  xor xor_4 (out_16, A2, B2);
  xor xor_5 (out_17, A1, B1);
  xor xor_6 (out_18, A0, B0);
endmodule

module Bitwise_not (
  input  in_1,
  input  in_2,
  input  in_3,
  input  in_4,
  input  in_5,
  input  in_6,
  output out_7,
  output out_8,
  output out_9,
  output out_10,
  output out_11,
  output out_12
);

  not not_1 (out_7, in_1);
  not not_2 (out_8, in_2);
  not not_3 (out_9, in_3);
  not not_4 (out_10, in_4);
  not not_5 (out_11, in_5);
  not not_6 (out_12, in_6);
endmodule

module Parity_Checker (
  input  A0,
  input  A1,
  input  A2,
  input  A3,
  input  A4,
  input  A5,
  output X
);

  wire xor_1_out, xor_2_out, xor_3_out, xor_4_out;

  xor xor_1 (xor_1_out, A0, A1);
  xor xor_2 (xor_2_out, xor_1_out, A2);
  xor xor_3 (xor_3_out, xor_2_out, A3);
  xor xor_4 (xor_4_out, xor_3_out, A4);
  xor xor_5 (X, xor_4_out, A5);

  // Notes on the sheet:
  //   0 FOR EVEN PARITY OR 1 FOR ODD PARITY
endmodule

module full_adder (
  input  in_1,
  input  in_2,
  input  in_3,
  output out_4,
  output out_5
);

  wire and_1_out, and_2_out, xor_1_out;

  xor xor_1 (xor_1_out, in_1, in_2);
  and and_1 (and_1_out, in_1, in_2);
  xor xor_2 (out_4, xor_1_out, in_3);
  and and_2 (and_2_out, xor_1_out, in_3);
  or or_1 (out_5, and_2_out, and_1_out);
endmodule

module Half_adder (
  input  in_1,
  input  in_2,
  output out_3,
  output out_4
);

  xor xor_1 (out_3, in_1, in_2);
  and and_1 (out_4, in_1, in_2);
endmodule

module Zero6 (
  input  [5:0] A,
  output Zero
);

  nor nor_1 (Zero, A[0], A[1], A[2], A[3], A[4], A[5]);

  // Notes on the sheet:
  //   Is Input Zero?
endmodule
